# Fritzing sketch systemeAlerte (saved by Fritzing 0.9.3b)
circuit board: 8.46667cm x 5.64444cm
breadboards: 1

parts:
  T-Cobbler1 = T-Cobbler
  module5 = Dule-Color LED
  module7 = Button
  module8 = IR Obstacle
  module9 = Buzzer
  module10 = I2C LCD1602

nets:
  VCC: T-Cobbler1.3V3#0, module7.VCC, module8.VCC, module9.VCC
  N1: T-Cobbler1.SDA1, module10.SDA
  N2: T-Cobbler1.SCL1, module10.SCL
  N3: T-Cobbler1.GPIO17, module8.SIG
  N4: T-Cobbler1.GPIO5, module5.R
  N5: T-Cobbler1.GPIO6, module5.G
  N6: T-Cobbler1.GPIO26, module9.SIG
  N7: T-Cobbler1.5V0#20, module10.VCC
  GND: T-Cobbler1.GND#22, module5.GND, module7.GND, module8.GND, module9.GND, module10.GND
  N8: T-Cobbler1.GPIO18, module7.SIG

notes:
  Button
  Dual-color LED
  IR Obstical Module
  Active Buzzer
  I2C LCD1602

custom parts:
  T-Cobbler: T-Cobbler for RPi B+ and Rpi2 from SunFounder
  Dule-Color LED: DuleColor LED module of SunFounder Sensor Kit
  Button: Button module of SunFounder Sensor Kit
  IR Obstacle: IR Obstacle module of SunFounder Sensor Kit.
  Buzzer: Buzzer module of SunFounder Sensor Kit
  I2C LCD1602: I2C LCD1602 module of SunFounder Sensor Kit
